# Fritzing sketch raspberry display arduino micro striscia led ventola modulo relè (saved by Fritzing 0.9.3b)

parts:
  Raspberry_Pi_1 = Raspberry Pi 3 [part_number=RPI-3-V1.2]
  VCC1 = 4 x AAA Battery Mount
  JP1 = USB_MICROB_PLUG [package=micro-b-ra-th]
  JP2 = USB_MICROB_PLUG [package=micro-b-ra-th]
  Componente1 = Arduino Nano (Rev3.0)
  JP3 = USB_MICROB_PLUG [package=micro-b-ra-th]
  JP4 = USB_MICROB_PLUG [package=micro-b-ra-th]
  S1 = Round Pushbutton
  U1 = 2-Channel 5v Relay Shield [package=relay-2ch5v10a]
  U2 = BATTERY-2 [package=battery-aaa]
  VCC2 = Battery
  R1 = Resistor [tolerance=±5% resistance=470 package="2010 [SMD]"]
  R2 = Resistor [tolerance=±5% resistance=100k package="2010 [SMD]"]
  R3 = Resistor [tolerance=±5% resistance=100k package="2010 [SMD]"]
  R4 = Resistor [tolerance=±5% resistance=100k package="2010 [SMD]"]
  R5 = Resistor [tolerance=±5% resistance=100k package="2010 [SMD]"]
  R6 = Resistor [tolerance=±5% resistance=100k package="2010 [SMD]"]
  U3 = WS2812 RGB LED strip
  R7 = Resistor [tolerance=±5% resistance=220 package=THT]
  M1 = DC Motor

nets:
  N1: Raspberry_Pi_1.GIPO4, S1.leg0, R6.Pin_1
  N2: Raspberry_Pi_1.3V3, S1.leg1
  N3: Raspberry_Pi_1.GIPO5, Componente1.A4, R5.Pin_1
  N4: Raspberry_Pi_1.GIPO6, Componente1.A5, R2.Pin_1
  N5: Raspberry_Pi_1.GIPO13, Componente1.A6, R4.Pin_1
  N6: Raspberry_Pi_1.GIPO19, U1.IN1, R7.Pin_0
  N7: Raspberry_Pi_1.GIPO26, Componente1.A3, R3.Pin_1
  GND: Raspberry_Pi_1.GND, VCC1.-, Componente1.GND, U1.GND, R2.Pin_0, R3.Pin_0, R4.Pin_0, R5.Pin_0, R6.Pin_0, U3.GND
  5V: Raspberry_Pi_1.5V, VCC1.+, Componente1.5V, U1.VCC, U3.VCC, R7.Pin_1
  VCC: JP1.VCC, JP2.VCC
  N8: JP1.D-, JP2.D-
  N9: JP1.D+, JP2.D+
  N10: JP1.ID, JP2.ID
  N11: Componente1.D9, R1.Pin_0
  VCC_2: JP3.VCC, JP4.VCC
  N12: JP3.D-, JP4.D-
  N13: JP3.D+, JP4.D+
  N14: JP3.ID, JP4.ID
  GND_2: JP3.GND, JP4.GND
  N15: U1.K1-In, VCC2.+
  N16: U1.K1-On, U1.K2-In, U1.K2-Off, U1.K2-On
  N17: U2.-1, M1.pin_2
  N18: U2.+1, VCC2.-
  N19: R1.Pin_1, U3.DIN

custom parts:
  2-Channel 5v Relay Shield: 2 Channel 5v Relay Shield w. 2x SPD-06VDC-SD-C
  WS2812 RGB LED strip: WS2812 strip
