# Fritzing sketch telecomando schema (saved by Fritzing 0.9.3b)

parts:
  VCC1 = 4 x AAA Battery Mount
  S1 = SPST Switch [package=r_sw_th]
  WeMos_D1_Mini1 = WeMos D1 Mini
  S2 = Pushbutton [package="[THT]"]
  S3 = Pushbutton [package="[THT]"]
  S4 = Pushbutton [package="[THT]"]
  S5 = Pushbutton [package="[THT]"]
  LED1 = smd LED [color="Red (633nm)" package="1206 [SMD]"]
  R1 = Resistor [tolerance=±5% resistance=680 package=THT]
  R2 = Resistor [tolerance=±5% resistance=100k package=THT]
  R3 = Resistor [tolerance=±5% resistance=100k package=THT]
  R4 = Resistor [tolerance=±5% resistance=100k package=THT]
  R5 = Resistor [tolerance=±5% resistance=100k package=THT]

nets:
  N1: VCC1.-, WeMos_D1_Mini1.G, R1.Pin_1, R2.Pin_1, R3.Pin_1, R4.Pin_1, R5.Pin_1
  N2: VCC1.+, S1.P
  N3: S1.S, WeMos_D1_Mini1.5V
  N4: WeMos_D1_Mini1.3V3, S2.Pin_1, S2.Pin_2, S3.Pin_1, S3.Pin_2, S4.Pin_1, S5.Pin_1
  N5: WeMos_D1_Mini1.D3, LED1.anode
  N6: WeMos_D1_Mini1.D5, S2.Pin_3, S2.Pin_4, R2.Pin_0
  N7: WeMos_D1_Mini1.D6, S3.Pin_3, S3.Pin_4, R3.Pin_0
  N8: WeMos_D1_Mini1.D7, S4.Pin_3, S4.Pin_4, R4.Pin_0
  N9: WeMos_D1_Mini1.D8, S5.Pin_3, S5.Pin_4, R5.Pin_0
  N10: LED1.cathode, R1.Pin_0
